// Logisim project Parie1.circ as structural Verilog: 6 circuits, main circuit unité de calcul PARTIE 1
module \unité_de_calcul_PARTIE_1  (
  input  [7:0] in_1,
  input  [7:0] in_2,
  input  [7:0] in_3,
  input  in_4,
  output [7:0] out_5,
  output out_6
);

  wire adder_1_cout, soustracteur_en_valeur_absolut_1_out_4;
  wire [7:0] adder_1_out, divider_1_out, divider_1_rem, multiplier_1_cout, multiplier_1_out,
       soustracteur_en_valeur_absolut_1_out_3, \valideur_d_octét_1_out_3 ;

  \Valideur_d_octét  \valideur_d_octét_1  (.in_2(in_4), .in_1(in_3), .out_3(\valideur_d_octét_1_out_3 ));
  Adder adder_1 (.a(in_1), .b(in_2), .out(adder_1_out), .cout(adder_1_cout));  // open: cin
  Soustracteur_en_valeur_absolut soustracteur_en_valeur_absolut_1 (
    .in_1(in_1), .in_2(in_2), .out_3(soustracteur_en_valeur_absolut_1_out_3),
    .out_4(soustracteur_en_valeur_absolut_1_out_4));
  \Séquenseur_interne  \séquenseur_interne_1  (
    .in_9(\valideur_d_octét_1_out_3 [0]), .in_10(\valideur_d_octét_1_out_3 [1]),
    .in_11(\valideur_d_octét_1_out_3 [2]), .in_1(adder_1_cout),
    .in_2(soustracteur_en_valeur_absolut_1_out_4), .in_3(multiplier_1_cout), .in_4(divider_1_rem),
    .in_5(adder_1_out), .in_6(soustracteur_en_valeur_absolut_1_out_3), .in_7(multiplier_1_out),
    .in_8(divider_1_out), .out_12(out_5), .out_13(out_6));
  Multiplier multiplier_1 (.a(in_1), .b(in_2), .out(multiplier_1_out), .cout(multiplier_1_cout));  // open: cin
  Divider divider_1 (.a(in_1), .b(in_2), .out(divider_1_out), .rem(divider_1_rem));  // open: upper
endmodule

module \Séquenseur_interne  (
  input  in_1,
  input  in_2,
  input  [7:0] in_3,
  input  [7:0] in_4,
  input  [7:0] in_5,
  input  [7:0] in_6,
  input  [7:0] in_7,
  input  [7:0] in_8,
  input  in_9,
  input  in_10,
  input  in_11,
  output [7:0] out_12,
  output out_13
);

  wire and_1_out, and_2_out, and_3_out, and_4_out, and_5_out, and_6_out, and_7_out, and_8_out, and_9_out,
       nor_1_p3, nor_1_p4, nor_2_out, nor_3_out, not_1_out, or_1_out, or_2_out, undriven, undriven_2;
  wire [7:0] \valideur_d_octét_1_out_3 , \valideur_d_octét_2_out_3 , \valideur_d_octét_3_out_3 ,
       \valideur_d_octét_4_out_3 ;

  and and_1 (and_1_out, in_9, in_10, undriven);
  // NOR_Gate nor_1: pin names not known; wires that end beside it: in_10, in_11, nor_1_p3, nor_1_p4, in_9
  nor nor_2 (nor_2_out, nor_1_p3, in_9, in_11);
  or or_1 (or_1_out, in_3[7], in_3[6], in_3[5], in_3[4], in_3[3], in_3[2], in_3[1], in_3[0]);
  nor nor_3 (nor_3_out, in_10, undriven, in_10, in_10, nor_1_p4);
  not not_1 (not_1_out, in_11);
  and and_2 (and_2_out, in_9, nor_1_p4);
  and and_3 (and_3_out, in_10, nor_2_out, undriven_2);
  and and_4 (and_4_out, undriven_2, and_1_out, not_1_out);
  and and_5 (and_5_out, nor_3_out, in_11);
  and and_6 (and_6_out, in_1, and_2_out);
  or or_2 (or_2_out, in_4[7], in_4[6], in_4[5], in_4[4], in_4[3], in_4[2], in_4[1], in_4[0]);
  and and_7 (and_7_out, in_2, and_3_out);
  and and_8 (and_8_out, or_1_out, and_4_out);
  or or_3 (out_13, and_6_out, and_7_out, and_8_out, and_9_out);
  \Valideur_d_octét  \valideur_d_octét_1  (.in_2(and_3_out), .in_1(in_6), .out_3(\valideur_d_octét_1_out_3 ));
  \Valideur_d_octét  \valideur_d_octét_2  (.in_2(and_4_out), .in_1(in_7), .out_3(\valideur_d_octét_2_out_3 ));
  and and_9 (and_9_out, or_2_out, and_5_out);
  \Valideur_d_octét  \valideur_d_octét_3  (.in_2(and_2_out), .in_1(in_5), .out_3(\valideur_d_octét_3_out_3 ));
  \Valideur_d_octét  \valideur_d_octét_4  (.in_2(and_5_out), .in_1(in_8), .out_3(\valideur_d_octét_4_out_3 ));
  assign out_12 = \valideur_d_octét_3_out_3  | \valideur_d_octét_1_out_3  | \valideur_d_octét_2_out_3  | \valideur_d_octét_4_out_3 ;  // OR_Gate or_4, 8 bits wide
endmodule

module \Valideur_d_octét  (
  input  [7:0] in_1,
  input  in_2,
  output [7:0] out_3
);

  wire undriven, undriven_2, undriven_3, undriven_4, undriven_5, undriven_6, undriven_7;

  and and_1 (out_3[7], in_2, in_1[7], undriven);
  and and_2 (out_3[6], undriven, in_2, in_1[6], undriven_2);
  and and_3 (out_3[5], undriven_2, in_2, in_1[5], undriven_3);
  and and_4 (out_3[4], undriven_3, in_2, in_1[4], undriven_4);
  and and_5 (out_3[3], undriven_4, in_2, in_1[3], undriven_5);
  and and_6 (out_3[2], undriven_5, in_2, in_1[2], undriven_6);
  and and_7 (out_3[1], undriven_6, in_2, in_1[1], undriven_7);
  and and_8 (out_3[0], undriven_7, in_2, in_1[0]);
endmodule

// Soustracteur
module Soustracteur_en_valeur_absolut (
  input  [7:0] in_1,
  input  [7:0] in_2,
  output [7:0] out_3,
  output out_4
);

  wire [7:0] subtractor_1_out, subtractor_2_out;

  Comparator comparator_1 (.a(in_1), .b(in_2), .lt(out_4));  // open: gt, eq
  Subtractor subtractor_1 (.a(in_2), .b(in_1), .out(subtractor_1_out));  // open: bin, bout
  Subtractor subtractor_2 (.a(in_1), .b(in_2), .out(subtractor_2_out));  // open: bin, bout
  Multiplexer #(.width(8)) multiplexer_1 (
    .in0(subtractor_2_out), .in1(subtractor_1_out), .out(out_3), .sel(out_4));  // open: en
endmodule

module \unité_de_calcul_PARTIE_2  (
);

  wire clk, clr;
  wire [7:0] ram_1_data, register_1_q, register_2_q, register_3_q, \unité_de_calcul_partie_1_1_out_5 ;

  Button button_1 (.out(clr));
  Clock clock_1 (.out(clk));
  RAM ram_1 (.data(ram_1_data));  // open: addr, sel, clk, ld, clr
  Register register_1 (.D(ram_1_data), .en(1'b0), .Q(register_1_q));  // open: clk, clr
  Register register_2 (.D(ram_1_data), .en(1'b0), .Q(register_2_q));  // open: clk, clr
  Register register_3 (.D(ram_1_data), .en(1'b0), .Q(register_3_q));  // open: clk, clr
  \unité_de_calcul_PARTIE_1  \unité_de_calcul_partie_1_1  (
    .in_1(register_1_q), .in_2(register_2_q), .in_3(register_3_q), .out_5(\unité_de_calcul_partie_1_1_out_5 ));  // open: in_4, out_6
  Register register_4 (.D(\unité_de_calcul_partie_1_1_out_5 ), .en(1'b0), .Q(ram_1_data));  // open: clk, clr
endmodule

module Sequenseur_global (
  input  in_1,
  input  in_2,
  output out_3,
  output [7:0] out_4,
  output out_5,
  output out_6,
  output out_7,
  output out_8
);

  wire and_1_out, d_ff_1_qn;

  Counter counter_1 (.Q(out_4), .clk(in_1));  // open: load, D, count, carry, clr
  and and_1 (and_1_out, 1'b1, in_2);
  D_Flip_Flop d_ff_1 (.Q(out_5), .Qn(d_ff_1_qn), .preset(and_1_out));  // open: clk, D, en, reset
endmodule
